// Logisim project capstone-circuit.circ as structural Verilog: 6 circuits, main circuit main
module main (
);

  ALU alu_1 ();  // open: CF, A, B, Opcode, Result, ZF, SF
endmodule

module Logical_Unit (
  input  in_1,
  input  in_2,
  input  in_3,
  input  in_4,
  input  in_5,
  output out_6,
  output out_7,
  output out_8,
  output out_9,
  output out_10
);

  wire A___B_out, AB_out, Not_B_out;

  and AB (AB_out, in_1, in_2);
  or A___B (A___B_out, in_1, in_2);
  not Not_B (Not_B_out, in_2);
  and and_1 (out_6, AB_out, in_3);
  and and_2 (out_7, A___B_out, in_4);
  and and_3 (out_8, Not_B_out, in_5);

  assign out_9 = in_1;
  assign out_10 = in_2;
endmodule

module Full_Adder (
  input  in_1,
  input  in_2,
  input  in_3,
  input  in_4,
  output out_5,
  output out_6
);

  wire and_1_out, and_2_out, xor_1_out, xor_2_out;

  and and_1 (and_1_out, in_4, in_3, in_2);
  or or_1 (out_6, and_1_out, and_2_out);
  xor xor_1 (xor_1_out, in_2, in_3);
  and and_2 (and_2_out, in_4, xor_1_out, in_1);
  xor xor_2 (xor_2_out, in_1, xor_1_out);
  and and_3 (out_5, xor_2_out, in_4);
endmodule

module Decoder (
  input  in_1,
  input  in_2,
  output out_3,
  output out_4,
  output out_5,
  output out_6
);

  wire not_1_out, not_2_out;

  not not_1 (not_1_out, in_1);
  not not_2 (not_2_out, in_2);
  and and_1 (out_3, not_1_out, not_2_out);
  and and_2 (out_4, not_1_out, in_2);
  and and_3 (out_5, in_1, not_2_out);
  and and_4 (out_6, in_1, in_2);
endmodule

module _1bit_ALU (
  input  INVA,
  input  A,
  input  Carry_In,
  input  ENA,
  input  B,
  input  ENB,
  input  F0,
  input  F1,
  output Output,
  output Carry_Out
);

  wire and_1_out, and_2_out, DC_out_3, DC_out_4, DC_out_5, DC_out_6, FA_out_5, LU_out_6, LU_out_7, LU_out_8,
       LU_out_9, LU_out_10, xor_1_out;

  and and_1 (and_1_out, A, ENA);
  xor xor_1 (xor_1_out, INVA, and_1_out);
  and and_2 (and_2_out, B, ENB);
  Logical_Unit LU (
    .in_1(xor_1_out), .in_2(and_2_out), .out_6(LU_out_6), .out_7(LU_out_7), .out_8(LU_out_8),
    .out_9(LU_out_9), .out_10(LU_out_10), .in_3(DC_out_3), .in_4(DC_out_4), .in_5(DC_out_5));
  Decoder DC (.out_3(DC_out_3), .out_4(DC_out_4), .out_5(DC_out_5), .out_6(DC_out_6), .in_1(F0), .in_2(F1));
  Full_Adder FA (
    .in_2(LU_out_10), .in_3(LU_out_9), .in_4(DC_out_6), .in_1(Carry_In), .out_5(FA_out_5), .out_6(Carry_Out));
  or or_1 (Output, LU_out_6, LU_out_7, LU_out_8, FA_out_5);
endmodule

module ALU (
  input  [5:0] Opcode,
  input  [7:0] A,
  input  [7:0] B,
  output [7:0] Result,
  output SF,
  output ZF,
  output CF
);

  wire n1bit_alu_1_carry_out, n1bit_alu_2_carry_out, n1bit_alu_3_carry_out, n1bit_alu_4_carry_out,
       n1bit_alu_5_carry_out, n1bit_alu_6_carry_out, n1bit_alu_7_carry_out, not_1_out, not_2_out, not_3_out,
       not_4_out, not_5_out, not_6_out, not_7_out, not_8_out;

  _1bit_ALU u_1bit_alu_1 (
    .INVA(Opcode[1]), .A(A[0]), .ENA(Opcode[3]), .B(B[0]), .ENB(Opcode[2]), .F0(Opcode[5]), .F1(Opcode[4]),
    .Output(Result[0]), .Carry_Out(n1bit_alu_1_carry_out), .Carry_In(Opcode[0]));
  _1bit_ALU u_1bit_alu_2 (
    .INVA(Opcode[1]), .A(A[1]), .ENA(Opcode[3]), .B(B[1]), .ENB(Opcode[2]), .F0(Opcode[5]), .F1(Opcode[4]),
    .Output(Result[1]), .Carry_Out(n1bit_alu_2_carry_out), .Carry_In(n1bit_alu_1_carry_out));
  _1bit_ALU u_1bit_alu_3 (
    .INVA(Opcode[1]), .A(A[2]), .ENA(Opcode[3]), .B(B[2]), .ENB(Opcode[2]), .F0(Opcode[5]), .F1(Opcode[4]),
    .Output(Result[2]), .Carry_Out(n1bit_alu_3_carry_out), .Carry_In(n1bit_alu_2_carry_out));
  _1bit_ALU u_1bit_alu_4 (
    .INVA(Opcode[1]), .A(A[3]), .ENA(Opcode[3]), .B(B[3]), .ENB(Opcode[2]), .F0(Opcode[5]), .F1(Opcode[4]),
    .Output(Result[3]), .Carry_Out(n1bit_alu_4_carry_out), .Carry_In(n1bit_alu_3_carry_out));
  _1bit_ALU u_1bit_alu_5 (
    .INVA(Opcode[1]), .A(A[4]), .ENA(Opcode[3]), .B(B[4]), .ENB(Opcode[2]), .F0(Opcode[5]), .F1(Opcode[4]),
    .Output(Result[4]), .Carry_Out(n1bit_alu_5_carry_out), .Carry_In(n1bit_alu_4_carry_out));
  _1bit_ALU u_1bit_alu_6 (
    .INVA(Opcode[1]), .A(A[5]), .ENA(Opcode[3]), .B(B[5]), .ENB(Opcode[2]), .F0(Opcode[5]), .F1(Opcode[4]),
    .Output(Result[5]), .Carry_Out(n1bit_alu_6_carry_out), .Carry_In(n1bit_alu_5_carry_out));
  _1bit_ALU u_1bit_alu_7 (
    .INVA(Opcode[1]), .A(A[6]), .ENA(Opcode[3]), .B(B[6]), .ENB(Opcode[2]), .F0(Opcode[5]), .F1(Opcode[4]),
    .Output(Result[6]), .Carry_Out(n1bit_alu_7_carry_out), .Carry_In(n1bit_alu_6_carry_out));
  _1bit_ALU u_1bit_alu_8 (
    .INVA(Opcode[1]), .A(A[7]), .ENA(Opcode[3]), .B(B[7]), .ENB(Opcode[2]), .F0(Opcode[5]), .F1(Opcode[4]),
    .Output(Result[7]), .Carry_Out(CF), .Carry_In(n1bit_alu_7_carry_out));
  not not_1 (not_1_out, Result[6]);
  not not_2 (not_2_out, Result[4]);
  not not_3 (not_3_out, Result[5]);
  not not_4 (not_4_out, Result[7]);
  and and_1 (ZF, not_4_out, not_1_out, not_3_out, not_2_out, not_8_out, not_6_out, not_5_out, not_7_out);
  not not_5 (not_5_out, Result[1]);
  not not_6 (not_6_out, Result[2]);
  not not_7 (not_7_out, Result[0]);
  not not_8 (not_8_out, Result[3]);

  assign SF = Result[7];
endmodule
